// Logisim project ping-pong.circ as structural Verilog: 9 circuits, main circuit movePoint
// 0xd
module movePoint (
  output out_1,
  output out_2,
  output out_3,
  output out_4
);

  wire and_1_out, and_2_out, and_5_out, and_6_out, and_7_out, and_8_out, and_9_out, and_10_out, and_11_out,
       and_12_out, bot_enabled, comparator_5_eq, comparator_6_eq, comparator_7_eq, comparator_8_eq,
       comparator_9_eq, comparator_10_eq, comparator_11_eq, comparator_12_eq, comparator_14_eq,
       comparator_15_eq, comparator_16_eq, comparator_17_eq, comparator_18_eq, comparator_19_eq,
       comparator_20_eq, comparator_21_eq, comparator_22_eq, d_ff_2_q, d_ff_7_q, fail1, fail2,
       frequency_divider_1_out, frequency_divider_2_out, frequency_divider_3_out, frequency_divider_4_out,
       frequency_divider_6_out, frequency_divider_7_out, gameover, is_ball_16, isDown, isLeft, kpower,
       l_button, lose, not_1_out, not_2_out, not_3_out, not_4_out, not_5_out, not_6_out, not_7_out,
       not_8_out, not_9_out, not_10_out, not_11_out, not_12_out, not_13_out, not_14_out, not_15_out,
       not_16_out, not_17_out, not_18_out, not_19_out, o_button, or_1_out, or_2_out, or_3_out, or_4_out,
       or_7_out, or_10_out, or_11_out, or_12_out, or_13_out, or_21_out, or_22_out, or_25_out, or_26_out,
       or_27_out, or_28_out, or_29_out, or_30_out, or_32_out, or_34_out, or_35_out, P, pause, playing, power,
       pull_resistor_2_node, r1, r2, restart, s_button, swap_x_dir_left_r_to_left,
       swap_x_dir_right_r_to_right, swap_x_direction_left_wall, swap_x_direction_right_wall, t_ff_1_q,
       transistor_1_out, transistor_3_out, w_button;
  wire [2:0] aoa, bruh;
  wire [3:0] bit_extender_1_out;
  wire [4:0] counter_1_q, counter_3_q, counter_4_q, dmx_x_cord;
  wire [6:0] keyboard;
  wire [7:0] multiplexer_4_out, multiplexer_5_out, multiplexer_37_out, p1_score_bin, p2_score_bin;
  wire [11:0] p1_score, p2_score;
  wire [30:1] decoder_3_out0, middle_rocket_pixel_left;
  wire [31:0] bot, cord1, cord2, cord11, cord22, D0, D1, D3, D5, D6, D7, D8, D9, D10, D11, D12, D13, D14,
       D15, D16, D17, D18, D19, D20, D21, D22, D23, D24, D25, D26, D28, D30, D31, demultiplexer_1_out3,
       demultiplexer_1_out28, dmx_y_cord, n0, n1, n2, n3, n4, n5, n6, n7, n8, n9, n10, n11, n12, n13, n14,
       n15, n16, n17, n18, n19, n20, n21, n22, n23, n24, n25, n26, n27, n28, n29, n30, n31, or_9_out,
       or_15_out, player1, player2, racket2, shifter_1_out, shifter_2_out, shifter_3_out, shifter_4_out,
       shifter_5_out, shifter_6_out, undriven, undriven_2, undriven_3, undriven_4, undriven_5, undriven_6,
       undriven_7, undriven_8, undriven_9, undriven_10, undriven_11, undriven_12, undriven_13, undriven_14,
       undriven_15, undriven_16, undriven_17, undriven_18, undriven_19, undriven_20, undriven_21,
       undriven_22, undriven_23, undriven_24, undriven_25, undriven_26, undriven_27, undriven_28,
       undriven_29, undriven_30, y_pause_cord;

  Hex_Digit_Display hex_digit_display_1 (.value(p1_score[11:8]));  // open: dp
  Hex_Digit_Display hex_digit_display_2 (.value(p1_score[7:4]));  // open: dp
  Hex_Digit_Display hex_digit_display_3 (.value(p1_score[3:0]));  // open: dp
  DotMatrix #(.matrixcols(32), .matrixrows(32)) dotmatrix_1 (
    .col0(n0), .col1(n1), .col2(n2), .col3(n3), .col4(n4), .col5(n5), .col6(n6), .col7(n7), .col8(n8),
    .col9(n9), .col10(n10), .col11(n11), .col12(n12), .col13(n13), .col14(n14), .col15(n15), .col16(n16),
    .col17(n17), .col18(n18), .col19(n19), .col20(n20), .col21(n21), .col22(n22), .col23(n23), .col24(n24),
    .col25(n25), .col26(n26), .col27(n27), .col28(n28), .col29(n29), .col30(n30), .col31(n31));
  Keyboard #(.buflen(1)) keyboard_1 (.clk(kpower), .data(keyboard));  // open: re, clr, avail
  Hex_Digit_Display hex_digit_display_4 (.value(p2_score[7:4]));  // open: dp
  Hex_Digit_Display hex_digit_display_5 (.value(p2_score[11:8]));  // open: dp
  Hex_Digit_Display hex_digit_display_6 (.value(p2_score[3:0]));  // open: dp
  Hex_Digit_Display hex_digit_display_7 (.value(bit_extender_1_out));  // open: dp
  assign bit_extender_1_out = {{1{1'b0}}, bruh};  // Bit_Extender bit_extender_1
  or or_1 (or_1_out, restart, isDown);
  not not_1 (not_1_out, restart);
  D_Flip_Flop d_ff_1 (.Q(isDown), .preset(dmx_y_cord[31]), .reset(dmx_y_cord[0]));  // open: clk, D, Qn, en
  Counter #(.width(5), .max('h1f)) counter_1 (
    .load(or_1_out), .D(5'b01111), .count(not_1_out), .Q(counter_1_q), .clk(or_2_out));  // open: carry, clr
  or or_2 (or_2_out, restart, frequency_divider_2_out);
  Decoder #(.select(5)) decoder_1 (
    .out0(dmx_y_cord[0]), .out1(dmx_y_cord[1]), .out2(dmx_y_cord[2]), .out3(dmx_y_cord[3]),
    .out4(dmx_y_cord[4]), .out5(dmx_y_cord[5]), .out6(dmx_y_cord[6]), .out7(dmx_y_cord[7]),
    .out8(dmx_y_cord[8]), .out9(dmx_y_cord[9]), .out10(dmx_y_cord[10]), .out11(dmx_y_cord[11]),
    .out12(dmx_y_cord[12]), .out13(dmx_y_cord[13]), .out14(dmx_y_cord[14]), .out15(dmx_y_cord[15]),
    .out16(dmx_y_cord[16]), .out17(dmx_y_cord[17]), .out18(dmx_y_cord[18]), .out19(dmx_y_cord[19]),
    .out20(dmx_y_cord[20]), .out21(dmx_y_cord[21]), .out22(dmx_y_cord[22]), .out23(dmx_y_cord[23]),
    .out24(dmx_y_cord[24]), .out25(dmx_y_cord[25]), .out26(dmx_y_cord[26]), .out27(dmx_y_cord[27]),
    .out28(dmx_y_cord[28]), .out29(dmx_y_cord[29]), .out30(dmx_y_cord[30]), .out31(dmx_y_cord[31]),
    .sel(counter_1_q));  // open: en
  Multiplexer #(.width(32)) multiplexer_1 (.in0(player2), .in1(bot), .out(racket2), .sel(bot_enabled));  // open: en
  Multiplexer #(.select(2), .width(32), .enable("false")) multiplexer_2 (
    .in0(32'h6e3000), .in1(D12), .in2(undriven), .in3(D12), .out(n12), .sel({pause, playing}));
  Multiplexer #(.select(2), .width(32), .enable("false")) multiplexer_3 (
    .in0(32'h924400), .in1(D16), .in2(undriven_2), .in3(D16), .out(n16), .sel({pause, playing}));
  // Probe on keyboard
  // Probe on keyboard
  // Probe on keyboard
  // Probe on keyboard
  D_Flip_Flop d_ff_2 (.Q(d_ff_2_q), .preset(or_3_out), .reset(or_4_out));  // open: clk, D, Qn, en
  or or_3 (or_3_out, swap_x_dir_left_r_to_left, swap_x_direction_right_wall);
  or or_4 (or_4_out, swap_x_direction_left_wall, swap_x_dir_right_r_to_right);
  Multiplexer #(.select(3), .width(8)) multiplexer_4 (
    .in0(8'h2), .in1(8'h3), .in2(8'h4), .in3(8'h6), .in4(8'h8), .in5(8'hc), .out(multiplexer_4_out), .sel(aoa));  // open: in6, in7, en
  assign D3 = player1 | demultiplexer_1_out3;  // OR_Gate or_5, 32 bits wide
  Comparator #(.width(7)) comparator_1 (.a(keyboard), .b(7'b1110111), .eq(w_button));  // open: gt, lt
  Comparator #(.width(7)) comparator_2 (.a(keyboard), .b(7'b1110011), .eq(s_button));  // open: gt, lt
  Comparator #(.width(7)) comparator_3 (.a(keyboard), .b(7'b1101111), .eq(o_button));  // open: gt, lt
  Comparator #(.width(7)) comparator_4 (.a(keyboard), .b(7'b1101100), .eq(l_button));  // open: gt, lt
  Multiplexer #(.select(3), .width(8)) multiplexer_5 (
    .in0(8'hc), .in1(8'h8), .in2(8'h6), .in3(8'h4), .in4(8'h3), .in5(8'h2), .out(multiplexer_5_out), .sel(aoa));  // open: in6, in7, en
  or or_6 (isLeft, restart, d_ff_2_q);
  not not_2 (not_2_out, restart);
  or or_7 (or_7_out, frequency_divider_1_out, restart);
  frequency_divider frequency_divider_1 (.IN(power), .OUT(frequency_divider_1_out), .n(multiplexer_4_out));  // open: _0
  Shifter #(.width(32)) shifter_1 (.in(dmx_y_cord), .\dist (5'b00001), .out(shifter_1_out));
  Shifter #(.width(32), .shift("lr")) shifter_2 (.in(dmx_y_cord), .\dist (5'b00001), .out(shifter_2_out));
  Multiplexer #(.select(2), .width(32), .enable("false")) multiplexer_6 (
    .in0({32{1'b0}}), .in1(D0), .in2(undriven_3), .in3(D0), .out(n0), .sel({pause, playing}));
  Multiplexer #(.select(2), .width(32), .enable("false")) multiplexer_7 (
    .in0(32'hfe3200), .in1(cord1), .in2(undriven_5), .in3(cord1), .out(n4), .sel({pause, playing}));
  Multiplexer #(.select(2), .width(32), .enable("false")) multiplexer_8 (
    .in0({32{1'b0}}), .in1(D8), .in2(undriven_6), .in3(D8), .out(n8), .sel({pause, playing}));
  Multiplexer #(.select(2), .width(32), .enable("false")) multiplexer_9 (
    .in0({32{1'b0}}), .in1(D13), .in2(undriven_4), .in3(D13), .out(n13), .sel({pause, playing}));
  Multiplexer #(.select(2), .width(32), .enable("false")) multiplexer_10 (
    .in0(32'h922200), .in1(D20), .in2(undriven_7), .in3(D20), .out(n20), .sel({pause, playing}));
  Multiplexer #(.select(2), .width(32), .enable("false")) multiplexer_11 (
    .in0(32'h647f00), .in1(D24), .in2(undriven_8), .in3(D24), .out(n24), .sel({pause, playing}));
  Multiplexer #(.select(2), .width(32), .enable("false")) multiplexer_12 (
    .in0({32{1'b0}}), .in1(D28), .in2(undriven_9), .in3(D28), .out(n28), .sel({pause, playing}));
  frequency_divider frequency_divider_2 (.IN(power), .OUT(frequency_divider_2_out), .n(multiplexer_5_out));  // open: _0
  Counter #(.width(5), .max('h1f)) counter_2 (
    .load(isLeft), .D(5'b01111), .count(not_2_out), .Q(dmx_x_cord), .clk(or_7_out));  // open: carry, clr
  assign bot = shifter_1_out | dmx_y_cord | shifter_2_out;  // OR_Gate or_8, 32 bits wide
  Demultiplexer #(.select(5), .width(32)) demultiplexer_1 (
    .out0(D0), .out1(D1), .out2(cord11), .out3(demultiplexer_1_out3), .out4(cord1), .out5(D5), .out6(D6),
    .out7(D7), .out8(D8), .out9(D9), .out10(D10), .out11(D11), .out12(D12), .out13(D13), .out14(D14),
    .out15(D15), .out16(D16), .out17(D17), .out18(D18), .out19(D19), .out20(D20), .out21(D21), .out22(D22),
    .out23(D23), .out24(D24), .out25(D25), .out26(D26), .out27(cord2), .out28(demultiplexer_1_out28),
    .out29(cord22), .out30(D30), .out31(D31), .in(dmx_y_cord), .sel(dmx_x_cord));  // open: en
  assign or_9_out = y_pause_cord | D17;  // OR_Gate or_9, 32 bits wide
  or or_10 (or_10_out, s_button, restart);
  not not_3 (not_3_out, restart);
  or or_11 (or_11_out, w_button, restart, s_button);
  or or_12 (or_12_out, l_button, restart);
  not not_4 (not_4_out, restart);
  or or_13 (or_13_out, o_button, restart, l_button);
  Multiplexer #(.select(2), .width(32), .enable("false")) multiplexer_13 (
    .in0({32{1'b0}}), .in1(D1), .in2(undriven_10), .in3(D1), .out(n1), .sel({pause, playing}));
  Multiplexer #(.select(2), .width(32), .enable("false")) multiplexer_14 (
    .in0(32'h904900), .in1(D5), .in2(undriven_11), .in3(D5), .out(n5), .sel({pause, playing}));
  Multiplexer #(.select(2), .width(32), .enable("false")) multiplexer_15 (
    .in0(32'hfe7f00), .in1(D9), .in2(undriven_12), .in3(D9), .out(n9), .sel({pause, playing}));
  Multiplexer #(.select(2), .width(32), .enable("false")) multiplexer_16 (
    .in0(32'h923f00), .in1(D17), .in3(or_9_out), .out(n17), .sel({pause, playing}));  // open: in2
  Multiplexer #(.select(2), .width(32), .enable("false")) multiplexer_17 (
    .in0(32'h924100), .in1(D21), .in2(undriven_13), .in3(D21), .out(n21), .sel({pause, playing}));
  Multiplexer #(.select(2), .width(32), .enable("false")) multiplexer_18 (
    .in0(32'h924900), .in1(D25), .in2(undriven_14), .in3(D25), .out(n25), .sel({pause, playing}));
  Multiplexer #(.select(2), .width(32), .enable("false")) multiplexer_19 (
    .in0({32{1'b0}}), .in1(cord22), .in2(undriven_15), .in3(cord22), .out(n29), .sel({pause, playing}));
  Counter #(.width(5), .max('h1d), .ongoal("stay")) counter_3 (
    .load(or_10_out), .D(5'b01111), .count(not_3_out), .Q(counter_3_q), .clk(or_11_out));  // open: carry, clr
  Counter #(.width(5), .max('h1d), .ongoal("stay")) counter_4 (
    .load(or_12_out), .D(5'b01111), .count(not_4_out), .Q(counter_4_q), .clk(or_13_out));  // open: carry, clr
  assign D28 = racket2 | demultiplexer_1_out28;  // OR_Gate or_14, 32 bits wide
  assign or_15_out = y_pause_cord | D14;  // OR_Gate or_15, 32 bits wide
  Decoder #(.select(5)) decoder_2 (
    .out0(middle_rocket_pixel_left[1]), .out1(middle_rocket_pixel_left[2]),
    .out2(middle_rocket_pixel_left[3]), .out3(middle_rocket_pixel_left[4]),
    .out4(middle_rocket_pixel_left[5]), .out5(middle_rocket_pixel_left[6]),
    .out6(middle_rocket_pixel_left[7]), .out7(middle_rocket_pixel_left[8]),
    .out8(middle_rocket_pixel_left[9]), .out9(middle_rocket_pixel_left[10]),
    .out10(middle_rocket_pixel_left[11]), .out11(middle_rocket_pixel_left[12]),
    .out12(middle_rocket_pixel_left[13]), .out13(middle_rocket_pixel_left[14]),
    .out14(middle_rocket_pixel_left[15]), .out15(middle_rocket_pixel_left[16]),
    .out16(middle_rocket_pixel_left[17]), .out17(middle_rocket_pixel_left[18]),
    .out18(middle_rocket_pixel_left[19]), .out19(middle_rocket_pixel_left[20]),
    .out20(middle_rocket_pixel_left[21]), .out21(middle_rocket_pixel_left[22]),
    .out22(middle_rocket_pixel_left[23]), .out23(middle_rocket_pixel_left[24]),
    .out24(middle_rocket_pixel_left[25]), .out25(middle_rocket_pixel_left[26]),
    .out26(middle_rocket_pixel_left[27]), .out27(middle_rocket_pixel_left[28]),
    .out28(middle_rocket_pixel_left[29]), .out29(middle_rocket_pixel_left[30]), .sel(counter_3_q));  // open: out30, out31, en
  Decoder #(.select(5)) decoder_3 (
    .out0(decoder_3_out0[1]), .out1(decoder_3_out0[2]), .out2(decoder_3_out0[3]), .out3(decoder_3_out0[4]),
    .out4(decoder_3_out0[5]), .out5(decoder_3_out0[6]), .out6(decoder_3_out0[7]), .out7(decoder_3_out0[8]),
    .out8(decoder_3_out0[9]), .out9(decoder_3_out0[10]), .out10(decoder_3_out0[11]),
    .out11(decoder_3_out0[12]), .out12(decoder_3_out0[13]), .out13(decoder_3_out0[14]),
    .out14(decoder_3_out0[15]), .out15(decoder_3_out0[16]), .out16(decoder_3_out0[17]),
    .out17(decoder_3_out0[18]), .out18(decoder_3_out0[19]), .out19(decoder_3_out0[20]),
    .out20(decoder_3_out0[21]), .out21(decoder_3_out0[22]), .out22(decoder_3_out0[23]),
    .out23(decoder_3_out0[24]), .out24(decoder_3_out0[25]), .out25(decoder_3_out0[26]),
    .out26(decoder_3_out0[27]), .out27(decoder_3_out0[28]), .out28(decoder_3_out0[29]),
    .out29(decoder_3_out0[30]), .sel(counter_4_q));  // open: out30, out31, en
  // Probe on racket2
  // Probe on player1
  Multiplexer #(.select(2), .width(32), .enable("false")) multiplexer_20 (
    .in0({32{1'b0}}), .in1(cord11), .in2(undriven_17), .in3(cord11), .out(n2), .sel({pause, playing}));
  Multiplexer #(.select(2), .width(32), .enable("false")) multiplexer_21 (
    .in0(32'h904900), .in1(D6), .in2(undriven_18), .in3(D6), .out(n6), .sel({pause, playing}));
  Multiplexer #(.select(2), .width(32), .enable("false")) multiplexer_22 (
    .in0(32'h904800), .in1(D10), .in2(undriven_19), .in3(D10), .out(n10), .sel({pause, playing}));
  Multiplexer #(.select(2), .width(32), .enable("false")) multiplexer_23 (
    .in0(32'hfe3f00), .in1(D14), .in3(or_15_out), .out(n14), .sel({pause, playing}));  // open: in2
  Multiplexer #(.select(2), .width(32), .enable("false")) multiplexer_24 (
    .in0({32{1'b0}}), .in1(D18), .in2(undriven_16), .in3(D18), .out(n18), .sel({pause, playing}));
  Multiplexer #(.select(2), .width(32), .enable("false")) multiplexer_25 (
    .in0(32'h4c4100), .in1(D22), .in2(undriven_20), .in3(D22), .out(n22), .sel({pause, playing}));
  Multiplexer #(.select(2), .width(32), .enable("false")) multiplexer_26 (
    .in0(32'h924900), .in1(D26), .in2(undriven_21), .in3(D26), .out(n26), .sel({pause, playing}));
  Multiplexer #(.select(2), .width(32), .enable("false")) multiplexer_27 (
    .in0({32{1'b0}}), .in1(D30), .in2(undriven_22), .in3(D30), .out(n30), .sel({pause, playing}));
  not not_5 (not_5_out, swap_x_direction_right_wall);
  Comparator #(.width(5)) comparator_5 (.a(dmx_x_cord), .b(5'b11101), .eq(comparator_5_eq));  // open: gt, lt
  not not_6 (not_6_out, swap_x_direction_left_wall);
  Comparator #(.width(5)) comparator_6 (.a(dmx_x_cord), .b({5{1'b0}}), .eq(comparator_6_eq));  // open: gt, lt
  Comparator #(.width(5)) comparator_7 (.a(dmx_x_cord), .b(5'b11101), .eq(comparator_7_eq));  // open: gt, lt
  not not_7 (not_7_out, swap_x_direction_right_wall);
  Comparator #(.width(5)) comparator_8 (.a(dmx_x_cord), .b({5{1'b0}}), .eq(comparator_8_eq));  // open: gt, lt
  not not_8 (not_8_out, swap_x_direction_left_wall);
  Comparator #(.mode("unsigned")) comparator_9 (.a(p1_score_bin), .b({8{1'b1}}), .eq(comparator_9_eq));  // open: gt, lt
  Comparator #(.mode("unsigned")) comparator_10 (
    .a({8{1'b1}}), .b(p2_score_bin), .eq(comparator_10_eq));  // open: gt, lt
  comp_y_cord comp_y_cord_1 (.in_1(racket2), .in_2(cord2), .\шарик (isDown), .out_4(r2));
  comp_y_cord comp_y_cord_2 (.in_1(player1), .in_2(cord1), .\шарик (isDown), .out_4(r1));
  and and_1 (and_1_out, not_5_out, comparator_5_eq);
  and and_2 (and_2_out, not_6_out, comparator_6_eq);
  Transistor #(.\type ("n")) transistor_1 (.in(not_7_out), .out(transistor_1_out), .gate(comparator_7_eq));
  Pull_Resistor pull_resistor_1 (.node(transistor_1_out));
  Pull_Resistor pull_resistor_2 (.node(pull_resistor_2_node));
  Transistor #(.\type ("n")) transistor_2 (.in(not_8_out), .out(pull_resistor_2_node), .gate(comparator_8_eq));
  or or_16 (gameover, comparator_9_eq, comparator_10_eq);
  Multiplexer #(.select(2), .width(32), .enable("false")) multiplexer_28 (
    .in0({32{1'b0}}), .in1(D3), .in2(undriven_23), .in3(D3), .out(n3), .sel({pause, playing}));
  Multiplexer #(.select(2), .width(32), .enable("false")) multiplexer_29 (
    .in0(32'h602600), .in1(D7), .in2(undriven_24), .in3(D7), .out(n7), .sel({pause, playing}));
  Multiplexer #(.select(2), .width(32), .enable("false")) multiplexer_30 (
    .in0(32'h904800), .in1(D11), .in2(undriven_25), .in3(D11), .out(n11), .sel({pause, playing}));
  Multiplexer #(.select(2), .width(32), .enable("false")) multiplexer_31 (
    .in0(32'h924400), .in1(D15), .in2(undriven_26), .in3(D15), .out(n15), .sel({pause, playing}));
  Multiplexer #(.select(2), .width(32), .enable("false")) multiplexer_32 (
    .in0(32'h641c00), .in1(D19), .in2(undriven_27), .in3(D19), .out(n19), .sel({pause, playing}));
  Multiplexer #(.select(2), .width(32), .enable("false")) multiplexer_33 (
    .in0({32{1'b0}}), .in1(D23), .in2(undriven_28), .in3(D23), .out(n23), .sel({pause, playing}));
  Multiplexer #(.select(2), .width(32), .enable("false")) multiplexer_34 (
    .in0(32'h4c4900), .in1(cord2), .in2(undriven_29), .in3(cord2), .out(n27), .sel({pause, playing}));
  Multiplexer #(.select(2), .width(32), .enable("false")) multiplexer_35 (
    .in0({32{1'b0}}), .in1(D31), .in2(undriven_30), .in3(D31), .out(n31), .sel({pause, playing}));
  or or_17 (swap_x_direction_right_wall, r2, fail2);
  or or_18 (swap_x_direction_left_wall, r1, fail1);
  // OR_Gate or_19 has open pins: in0=and_1_out, in1=and_2_out, out=open
  or or_20 (lose, transistor_1_out, pull_resistor_2_node);
  comp_y_cord comp_y_cord_3 (.in_1(player1), .in_2(cord11), .\шарик (isDown), .out_4(swap_x_dir_left_r_to_left));
  comp_y_cord comp_y_cord_4 (.in_1(racket2), .in_2(cord22), .\шарик (isDown), .out_4(swap_x_dir_right_r_to_right));
  Shifter #(.width(32)) shifter_3 (.in({1'b0, middle_rocket_pixel_left, 1'b0}), .\dist (5'b00001), .out(shifter_3_out));
  Shifter #(.width(32), .shift("lr")) shifter_4 (
    .in({1'b0, middle_rocket_pixel_left, 1'b0}), .\dist (5'b00001), .out(shifter_4_out));
  Shifter #(.width(32)) shifter_5 (.in({1'b0, decoder_3_out0, 1'b0}), .\dist (5'b00001), .out(shifter_5_out));
  Shifter #(.width(32), .shift("lr")) shifter_6 (
    .in({1'b0, decoder_3_out0, 1'b0}), .\dist (5'b00001), .out(shifter_6_out));
  frequency_divider frequency_divider_3 (.IN(kpower), .OUT(frequency_divider_3_out), .n({8{1'b1}}), ._0(or_21_out));
  or or_21 (or_21_out, w_button, frequency_divider_3_out);
  frequency_divider frequency_divider_4 (.IN(kpower), .OUT(frequency_divider_4_out), .n({8{1'b1}}), ._0(or_22_out));
  or or_22 (or_22_out, s_button, frequency_divider_4_out);
  assign player1 = shifter_3_out | {1'b0, middle_rocket_pixel_left, 1'b0} | shifter_4_out;  // OR_Gate or_23, 32 bits wide
  assign player2 = shifter_5_out | {1'b0, decoder_3_out0, 1'b0} | shifter_6_out;  // OR_Gate or_24, 32 bits wide
  Clock clock_1 (.out(kpower));
  D_Flip_Flop d_ff_3 (.clk(w_button), .D(w_button), .Q(out_1), .reset(or_25_out));  // open: Qn, preset, en
  or or_25 (or_25_out, frequency_divider_3_out, s_button);
  D_Flip_Flop d_ff_4 (.clk(s_button), .D(s_button), .Q(out_3), .reset(or_26_out));  // open: Qn, preset, en
  or or_26 (or_26_out, frequency_divider_4_out, w_button);
  // Probe on dmx_x_cord
  Counter #(.ongoal("continue")) counter_5 (
    .Q(p2_score_bin), .clk(fail1), .clr(restart));  // open: load, D, count, carry
  Counter #(.ongoal("continue")) counter_6 (
    .Q(p1_score_bin), .clk(fail2), .clr(restart));  // open: load, D, count, carry
  pause pause_1 (._14_y(D13), ._15_y(D14), ._13_y(D15), ._16_y(D16), ._18_y(D17), ._17_y(D18), .is_0_up(is_ball_16));
  Pull_Resistor pull_resistor_3 (.node(is_ball_16));
  // Probe on y_pause_cord
  Multiplexer #(.width(32)) multiplexer_36 (
    .in0(32'h1e), .in1(32'h78000000), .out(y_pause_cord), .sel(is_ball_16));  // open: en
  // Probe on keyboard
  nor nor_1 (fail1, dmx_x_cord[0], dmx_x_cord[1], dmx_x_cord[2], dmx_x_cord[3], dmx_x_cord[4]);
  and and_3 (fail2, dmx_x_cord[0], dmx_x_cord[1], dmx_x_cord[2], dmx_x_cord[3], dmx_x_cord[4]);
  bcd bcd_1 (._8bit_Input(p2_score_bin), .BCD_Output(p2_score));
  bcd bcd_2 (._8bit_Input(p1_score_bin), .BCD_Output(p1_score));
  Multiplexer #(.width(8)) multiplexer_37 (
    .in0(8'h5), .in1({8{1'b0}}), .out(multiplexer_37_out), .sel(pause));  // open: en
  frequency_divider frequency_divider_5 (.IN(transistor_3_out), .OUT(power), .n(multiplexer_37_out));  // open: _0
  Transistor #(.\type ("n")) transistor_3 (.in(kpower), .out(transistor_3_out), .gate(playing));
  // Probe on keyboard
  // Probe on keyboard
  Comparator #(.width(7)) comparator_11 (.a(keyboard), .b(7'b0100000), .eq(comparator_11_eq));  // open: gt, lt
  Comparator #(.width(7)) comparator_12 (.a(keyboard), .b(7'b1110000), .eq(comparator_12_eq));  // open: gt, lt
  Comparator #(.width(7)) comparator_13 (.a(keyboard), .b(7'b1110010), .eq(restart));  // open: gt, lt
  D_Flip_Flop d_ff_5 (.clk(o_button), .D(o_button), .Q(out_2), .reset(or_27_out));  // open: Qn, preset, en
  or or_27 (or_27_out, frequency_divider_6_out, l_button);
  frequency_divider frequency_divider_6 (.IN(kpower), .OUT(frequency_divider_6_out), .n({8{1'b1}}), ._0(or_28_out));
  or or_28 (or_28_out, o_button, frequency_divider_6_out);
  D_Flip_Flop d_ff_6 (.clk(l_button), .D(l_button), .Q(out_4), .reset(or_29_out));  // open: Qn, preset, en
  or or_29 (or_29_out, frequency_divider_7_out, o_button);
  frequency_divider frequency_divider_7 (.IN(kpower), .OUT(frequency_divider_7_out), .n({8{1'b1}}), ._0(or_30_out));
  or or_30 (or_30_out, l_button, frequency_divider_7_out);
  not not_9 (not_9_out, gameover);
  D_Flip_Flop d_ff_7 (
    .clk(comparator_11_eq), .D(comparator_11_eq), .Q(d_ff_7_q), .reset(restart));  // open: Qn, preset, en
  T_Flip_Flop t_ff_1 (.clk(comparator_12_eq), .T(comparator_12_eq), .Q(t_ff_1_q));  // open: Qn, preset, reset, en
  Comparator #(.width(5)) comparator_14 (.a(dmx_x_cord), .b(5'b00100), .eq(comparator_14_eq));  // open: gt, lt
  Comparator #(.width(5)) comparator_15 (.a(dmx_x_cord), .b(5'b00100), .eq(comparator_15_eq));  // open: gt, lt
  Comparator #(.width(5)) comparator_16 (.a(dmx_x_cord), .b(5'b11011), .eq(comparator_16_eq));  // open: gt, lt
  Comparator #(.width(5)) comparator_17 (.a(dmx_x_cord), .b(5'b11101), .eq(comparator_17_eq));  // open: gt, lt
  Comparator #(.width(5)) comparator_18 (.a(dmx_x_cord), .b(5'b00100), .eq(comparator_18_eq));  // open: gt, lt
  Comparator #(.width(5)) comparator_19 (.a(dmx_x_cord), .b(5'b00100), .eq(comparator_19_eq));  // open: gt, lt
  Comparator #(.width(5)) comparator_20 (.a(dmx_x_cord), .b(5'b11011), .eq(comparator_20_eq));  // open: gt, lt
  Comparator #(.width(5)) comparator_21 (.a(dmx_x_cord), .b(5'b11011), .eq(comparator_21_eq));  // open: gt, lt
  and and_4 (playing, not_9_out, d_ff_7_q);
  or or_31 (pause, t_ff_1_q, gameover);
  // Probe on keyboard
  Comparator #(.width(7)) comparator_22 (.a(keyboard), .b(7'b1100010), .eq(comparator_22_eq));  // open: gt, lt
  not not_10 (not_10_out, isDown);
  not not_11 (not_11_out, isLeft);
  not not_12 (not_12_out, isDown);
  not not_13 (not_13_out, isLeft);
  not not_14 (not_14_out, isDown);
  not not_15 (not_15_out, isDown);
  not not_16 (not_16_out, isLeft);
  not not_17 (not_17_out, isLeft);
  T_Flip_Flop t_ff_2 (.clk(comparator_22_eq), .T(comparator_22_eq), .Q(bot_enabled));  // open: Qn, preset, reset, en
  and and_5 (and_5_out, r1, isDown, out_1, comparator_14_eq, isLeft);
  and and_6 (and_6_out, r1, not_10_out, out_3, comparator_15_eq, isLeft);
  and and_7 (and_7_out, r2, isDown, out_2, comparator_16_eq, not_11_out);
  and and_8 (and_8_out, r2, not_12_out, out_4, comparator_17_eq, not_13_out);
  and and_9 (and_9_out, r1, not_14_out, out_1, comparator_18_eq, isLeft);
  and and_10 (and_10_out, r1, isDown, out_3, comparator_19_eq, isLeft);
  and and_11 (and_11_out, r2, not_15_out, out_2, comparator_20_eq, not_16_out);
  and and_12 (and_12_out, r2, isDown, out_4, comparator_21_eq, not_17_out);
  or or_32 (or_32_out, and_5_out, and_6_out, and_7_out, and_8_out);
  or or_33 (P, and_9_out, and_10_out, and_11_out, and_12_out);
  or or_34 (or_34_out, or_32_out, P);
  not not_18 (not_18_out, P);
  not not_19 (not_19_out, restart);
  Counter #(.width(3), .max('h5), .ongoal("stay")) counter_7 (
    .load(not_18_out), .D(3'b011), .count(not_19_out), .Q(aoa), .clk(or_35_out));  // open: carry, clr
  or or_35 (or_35_out, restart, or_34_out);

  // Other names for the same wires on the sheet: D4[31:0] = cord1; D27[31:0] = cord2; D2[31:0] = cord11;
  //   D29[31:0] = cord22; l_pressed = out_4; o_pressed = out_2; racket1[31:0] = player1; s_pressed = out_3;
  //   tunnel[1:0] = {pause, playing}; w_pressed = out_1

  // Notes on the sheet:
  //   SCORE
  //   Player 1
  //   Inputs
  //   Player 1 - W and S
  //   Player 2 - O and L
  //   Pause - P
  //   Restart - R
  //   Bot - B
  //   Start game - SPACE
  //   SCORE
  //   Player 2
  //   PRESS SPACE
  //   движение по оси y
  //   PLAYER_1
  //   PLAYER_2
  //   движение по оси x
  //   BOT (Skynet in future)
  //   Playing scene
  //   Scene select
  //   00 - start scene
  //   01 - playing scene
  //   10 - gameover scene
  //   11 - pause scene
  //   Keyboard input
  //   Keyboard input
  //   можно воткнуть сюда регистр
  //   Gameover check
  //   если попадание: правая стенка
  //   если попадание: левая стенка
  //   неработающие варианты проверки на столкновение
  //   отскок между ракеткой и стенкой
  //   Запоминание последней кнопки
  //   Goal check
  //   Score count and print
  //   Power
  //   pause screen
  //   запись координат паузы
  //   проверка на положение мяча
  //   Keyboard input
  //   уменьшение угла
  //   увеличение угла
  //   угол наклона мячика
endmodule

// ||
module comp_y_cord (
  input  [31:0] in_1,
  input  [31:0] in_2,
  input  \шарик ,
  output out_4
);

  wire or_1_out, or_2_out, or_3_out, or_4_out, or_5_out;
  wire [29:0] and_2_out, and_3_out;
  wire [31:0] and_1_out;

  assign and_1_out = in_1 & in_2;  // AND_Gate and_1, 32 bits wide
  assign and_2_out = in_1[30:1] & in_2[29:0];  // AND_Gate and_2, 30 bits wide
  or or_1 (or_1_out, and_1_out[0], and_1_out[1], and_1_out[2], and_1_out[3], and_1_out[4], and_1_out[5], and_1_out[6], and_1_out[7], and_1_out[8], and_1_out[9], and_1_out[10], and_1_out[11], and_1_out[12], and_1_out[13], and_1_out[14], and_1_out[15], and_1_out[17], and_1_out[18], and_1_out[19], and_1_out[20], and_1_out[21], and_1_out[22], and_1_out[23], and_1_out[24], and_1_out[25], and_1_out[26], and_1_out[27], and_1_out[28], and_1_out[29], and_1_out[30], and_1_out[31], and_1_out[16]);
  assign and_3_out = in_1[30:1] & in_2[31:2];  // AND_Gate and_3, 30 bits wide
  or or_2 (or_2_out, and_2_out[0], and_2_out[1], and_2_out[2], and_2_out[3], and_2_out[4], and_2_out[5], and_2_out[6], and_2_out[7], and_2_out[8], and_2_out[9], and_2_out[10], and_2_out[11], and_2_out[12], and_2_out[13], and_2_out[14], and_2_out[16], and_2_out[17], and_2_out[18], and_2_out[19], and_2_out[20], and_2_out[21], and_2_out[22], and_2_out[23], and_2_out[24], and_2_out[25], and_2_out[26], and_2_out[27], and_2_out[28], and_2_out[29], and_2_out[15]);
  or or_3 (or_3_out, and_3_out[0], and_3_out[1], and_3_out[2], and_3_out[3], and_3_out[4], and_3_out[5], and_3_out[6], and_3_out[7], and_3_out[8], and_3_out[9], and_3_out[10], and_3_out[11], and_3_out[12], and_3_out[13], and_3_out[14], and_3_out[16], and_3_out[17], and_3_out[18], and_3_out[19], and_3_out[20], and_3_out[21], and_3_out[22], and_3_out[23], and_3_out[24], and_3_out[25], and_3_out[26], and_3_out[27], and_3_out[28], and_3_out[29], and_3_out[15]);
  or or_4 (or_4_out, or_1_out, or_3_out);
  or or_5 (or_5_out, or_1_out, or_2_out);
  Multiplexer multiplexer_1 (.in0(or_5_out), .in1(or_4_out), .out(out_4), .sel(\шарик ));  // open: en

  // Other names for the same wires on the sheet: _0 = in_2[0]; ball_cord_y[31:0] = in_2; _1 = in_2[1];
  //   rock_cord_y[31:0] = in_1; _2 = in_2[2]; _3 = in_2[3]; _4 = in_2[4]; _5 = in_2[5]; _6 = in_2[6]; _7 = in_2[7];
  //   _8 = in_2[8]; _9 = in_2[9]; _10 = in_2[10]; _11 = in_2[11]; _12 = in_2[12]; _13 = in_2[13]; _14 = in_2[14];
  //   _15 = in_2[15]; _16 = in_2[16]; _17 = in_2[17]; _18 = in_2[18]; _19 = in_2[19]; _20 = in_2[20]; _21 = in_2[21];
  //   _22 = in_2[22]; _23 = in_2[23]; _24 = in_2[24]; _25 = in_2[25]; _26 = in_2[26]; _27 = in_2[27]; _28 = in_2[28];
  //   _29 = in_2[29]; _30 = in_2[30]; _31 = in_2[31]; _1_down = \шарик 

  // Notes on the sheet:
  //   ракетка
  //   снизу вверх
  //   сверху вниз
endmodule

module parseScore (
  input  [7:0] in_1,
  output [3:0] out_2,
  output [3:0] out_3,
  output [3:0] out_4
);

  wire [7:0] divider_1_out, divider_2_out, multiplier_1_out, multiplier_2_out, subtractor_1_out,
       subtractor_2_out;

  // Probe on in_1
  // Probe on divider_1_out
  Divider divider_1 (.a(in_1), .b(8'ha), .out(divider_1_out));  // open: upper, rem
  Divider divider_2 (.a(divider_1_out), .b(8'ha), .out(divider_2_out));  // open: upper, rem
  Multiplier multiplier_1 (.a(divider_1_out), .b(8'ha), .out(multiplier_1_out));  // open: cin, cout
  // Probe on multiplier_1_out
  // Probe on multiplier_2_out
  Multiplier multiplier_2 (.a(divider_2_out), .b(8'ha), .out(multiplier_2_out));  // open: cin, cout
  Bit_Extender #(.out_width(4)) bit_extender_1 (.in(divider_2_out), .out(out_2));
  Subtractor subtractor_1 (.a(in_1), .b(multiplier_1_out), .out(subtractor_1_out));  // open: bin, bout
  // Probe on out_2
  // Probe on subtractor_2_out
  Subtractor subtractor_2 (.a(divider_1_out), .b(multiplier_2_out), .out(subtractor_2_out));  // open: bin, bout
  // Probe on subtractor_1_out
  Bit_Extender #(.out_width(4)) bit_extender_2 (.in(subtractor_2_out), .out(out_3));
  Bit_Extender #(.out_width(4)) bit_extender_3 (.in(subtractor_1_out), .out(out_4));

  // Notes on the sheet:
  //   OBSOLETE
  //   as of v0.1.3
endmodule

module test (
  input  [31:0] bus_0
);

  wire comparator_1_eq, comparator_2_eq, or_1_out, power, restart;
  wire [2:0] counter_1_q;
  wire [6:0] keyboard;
  wire [7:0] middle_rocket_pixel_left, rocket1, shifter_1_out, shifter_2_out;
  wire [31:0] undriven, undriven_2, undriven_3, undriven_4, undriven_5, undriven_6, undriven_7, undriven_8,
       undriven_9, undriven_10, undriven_11, undriven_12, undriven_13, undriven_14, undriven_15, undriven_16,
       undriven_17, undriven_18, undriven_19, undriven_20, undriven_21, undriven_22, undriven_23,
       undriven_24, undriven_25, undriven_26, undriven_27, undriven_28, undriven_29, undriven_30;

  Keyboard #(.buflen(1)) keyboard_1 (.clk(power), .data(keyboard));  // open: re, clr, avail
  Clock clock_1 (.out(power));
  Button button_1 (.out(restart));
  // Probe on keyboard
  // Probe on keyboard
  DotMatrix #(.matrixcols(32), .matrixrows(32)) dotmatrix_1 (
    .col0(undriven), .col1(undriven_2), .col2(undriven_3), .col3(undriven_4), .col4(undriven_5),
    .col5(undriven_6), .col6(undriven_7), .col7(undriven_8), .col8(undriven_9), .col9(undriven_10),
    .col10(undriven_11), .col11(undriven_12), .col12(undriven_13), .col13(bus_0), .col14(undriven_14),
    .col15(undriven_15), .col16(bus_0), .col17(undriven_16), .col18(undriven_17), .col19(undriven_18),
    .col20(undriven_19), .col21(undriven_20), .col22(undriven_21), .col23(undriven_22), .col24(undriven_23),
    .col25(undriven_24), .col26(undriven_25), .col27(undriven_26), .col28(undriven_27), .col29(undriven_28),
    .col30(undriven_29), .col31(undriven_30));
  // Probe on bus_0
  Comparator #(.width(7)) comparator_1 (.a(keyboard), .b(7'b1110111), .eq(comparator_1_eq));  // open: gt, lt
  Comparator #(.width(7)) comparator_2 (.a(keyboard), .b(7'b1110011), .eq(comparator_2_eq));  // open: gt, lt
  Counter #(.width(3), .max('h7)) counter_1 (
    .load(comparator_2_eq), .Q(counter_1_q), .clk(or_1_out), .clr(restart));  // open: D, count, carry
  or or_1 (or_1_out, comparator_1_eq, comparator_2_eq);
  Decoder #(.select(3)) decoder_1 (
    .out0(middle_rocket_pixel_left[0]), .out1(middle_rocket_pixel_left[1]),
    .out2(middle_rocket_pixel_left[2]), .out3(middle_rocket_pixel_left[3]),
    .out4(middle_rocket_pixel_left[4]), .out5(middle_rocket_pixel_left[5]),
    .out6(middle_rocket_pixel_left[6]), .out7(middle_rocket_pixel_left[7]), .sel(counter_1_q));  // open: en
  Shifter shifter_1 (.in(middle_rocket_pixel_left), .\dist (3'b001), .out(shifter_1_out));
  Shifter #(.shift("lr")) shifter_2 (.in(middle_rocket_pixel_left), .\dist (3'b001), .out(shifter_2_out));
  assign rocket1 = shifter_1_out | middle_rocket_pixel_left | shifter_2_out;  // OR_Gate or_2, 8 bits wide

  // Notes on the sheet:
  //   Inputs
  //   w, s // o, l
endmodule

module frequency_divider (
  input  [7:0] n,
  input  IN,
  input  _0,
  output OUT
);

  wire comparator_1_eq, comparator_1_lt, or_1_out, or_2_out;
  wire [7:0] counter_1_q;

  Counter counter_1 (.count(IN), .Q(counter_1_q), .clk(IN), .clr(or_1_out));  // open: load, D, carry
  or or_1 (or_1_out, _0, or_2_out);
  Comparator #(.mode("unsigned")) comparator_1 (
    .a(n), .b(counter_1_q), .eq(comparator_1_eq), .lt(comparator_1_lt));  // open: gt
  or or_2 (or_2_out, comparator_1_eq, comparator_1_lt);
  T_Flip_Flop t_ff_1 (.clk(or_2_out), .T(or_2_out), .Q(OUT), .reset(_0));  // open: Qn, preset, en
endmodule

module bcd (
  input  [7:0] _8bit_Input,
  output [11:0] BCD_Output
);

  wire [3:0] bcd_helper_1_out, bcd_helper_2_out, bcd_helper_3_out, bcd_helper_4_out, bcd_helper_5_out,
       bcd_helper_6_out, bcd_helper_7_out, bcd_helper_8_out, bcd_helper_9_out, bcd_helper_10_out,
       bcd_helper_11_out, bcd_helper_12_out, bcd_helper_13_out, bcd_helper_14_out, bcd_helper_15_out,
       bcd_helper_16_out, bcd_helper_17_out, bcd_helper_18_out;
  wire [3:3] bcd_helper_21_out;

  // Probe on _8bit_Input
  bcd_helper bcd_helper_1 (.inp({3'b000, _8bit_Input[7]}), .out(bcd_helper_1_out));
  bcd_helper bcd_helper_2 (.inp(4'b0000), .out(bcd_helper_2_out));
  bcd_helper bcd_helper_3 (.inp(4'b0000), .out(bcd_helper_3_out));
  bcd_helper bcd_helper_4 (.inp({bcd_helper_1_out[2:0], _8bit_Input[6]}), .out(bcd_helper_4_out));
  bcd_helper bcd_helper_5 (.inp({bcd_helper_2_out[2:0], bcd_helper_1_out[3]}), .out(bcd_helper_5_out));
  bcd_helper bcd_helper_6 (.inp({bcd_helper_3_out[2:0], bcd_helper_2_out[3]}), .out(bcd_helper_6_out));
  bcd_helper bcd_helper_7 (.inp({bcd_helper_4_out[2:0], _8bit_Input[5]}), .out(bcd_helper_7_out));
  bcd_helper bcd_helper_8 (.inp({bcd_helper_5_out[2:0], bcd_helper_4_out[3]}), .out(bcd_helper_8_out));
  bcd_helper bcd_helper_9 (.inp({bcd_helper_6_out[2:0], bcd_helper_5_out[3]}), .out(bcd_helper_9_out));
  bcd_helper bcd_helper_10 (.inp({bcd_helper_7_out[2:0], _8bit_Input[4]}), .out(bcd_helper_10_out));
  bcd_helper bcd_helper_11 (.inp({bcd_helper_8_out[2:0], bcd_helper_7_out[3]}), .out(bcd_helper_11_out));
  bcd_helper bcd_helper_12 (.inp({bcd_helper_9_out[2:0], bcd_helper_8_out[3]}), .out(bcd_helper_12_out));
  bcd_helper bcd_helper_13 (.inp({bcd_helper_10_out[2:0], _8bit_Input[3]}), .out(bcd_helper_13_out));
  bcd_helper bcd_helper_14 (.inp({bcd_helper_11_out[2:0], bcd_helper_10_out[3]}), .out(bcd_helper_14_out));
  bcd_helper bcd_helper_15 (.inp({bcd_helper_12_out[2:0], bcd_helper_11_out[3]}), .out(bcd_helper_15_out));
  bcd_helper bcd_helper_16 (.inp({bcd_helper_13_out[2:0], _8bit_Input[2]}), .out(bcd_helper_16_out));
  bcd_helper bcd_helper_17 (.inp({bcd_helper_14_out[2:0], bcd_helper_13_out[3]}), .out(bcd_helper_17_out));
  bcd_helper bcd_helper_18 (.inp({bcd_helper_15_out[2:0], bcd_helper_14_out[3]}), .out(bcd_helper_18_out));
  bcd_helper bcd_helper_19 (.inp({bcd_helper_16_out[2:0], _8bit_Input[1]}), .out(BCD_Output[4:1]));
  bcd_helper bcd_helper_20 (.inp({bcd_helper_17_out[2:0], bcd_helper_16_out[3]}), .out(BCD_Output[8:5]));
  bcd_helper bcd_helper_21 (
    .inp({bcd_helper_18_out[2:0], bcd_helper_17_out[3]}), .out({bcd_helper_21_out[3], BCD_Output[11:9]}));
  // Probe on BCD_Output[11:8]
  // Probe on BCD_Output[7:4]
  // Probe on {BCD_Output[3:1], _8bit_Input[0]}

  assign BCD_Output[0] = _8bit_Input[0];

  // Notes on the sheet:
  //   The double dable algorithm
endmodule

module bcd_helper (
  input  [3:0] inp,
  output [3:0] out
);

  wire comparator_1_eq, comparator_1_lt, or_1_out;
  wire [3:0] adder_1_out;

  // Probe on inp
  Adder #(.width(4)) adder_1 (.a(4'b0011), .b(inp), .out(adder_1_out));  // open: cin, cout
  Comparator #(.width(4), .mode("unsigned")) comparator_1 (
    .a(4'b0101), .b(inp), .eq(comparator_1_eq), .lt(comparator_1_lt));  // open: gt
  or or_1 (or_1_out, comparator_1_eq, comparator_1_lt);
  Multiplexer #(.width(4)) multiplexer_1 (.in0(inp), .in1(adder_1_out), .out(out), .sel(or_1_out));  // open: en
endmodule

module pause (
  input  [31:0] _14_y,
  input  [31:0] _15_y,
  input  [31:0] _13_y,
  input  [31:0] _16_y,
  input  [31:0] _18_y,
  input  [31:0] _17_y,
  output is_0_up
);

  wire not_1_out, not_2_out, not_3_out, not_4_out, not_5_out, not_6_out, y_down_13, y_down_14, y_down_15,
       y_down_16, y_down_17, y_down_18, y_up_13, y_up_14, y_up_15, y_up_16, y_up_17, y_up_18;

  or or_1 (y_down_14, _14_y[0], _14_y[1], _14_y[2], _14_y[3], _14_y[4], _14_y[5], _14_y[6], _14_y[7], _14_y[8], _14_y[9], _14_y[10], _14_y[11], _14_y[12], _14_y[13], _14_y[14], _14_y[15]);
  or or_2 (y_up_14, _14_y[16], _14_y[17], _14_y[18], _14_y[19], _14_y[20], _14_y[21], _14_y[22], _14_y[23], _14_y[24], _14_y[25], _14_y[26], _14_y[27], _14_y[28], _14_y[29], _14_y[30], _14_y[31]);
  or or_3 (y_down_15, _15_y[0], _15_y[1], _15_y[2], _15_y[3], _15_y[4], _15_y[5], _15_y[6], _15_y[7], _15_y[8], _15_y[9], _15_y[10], _15_y[11], _15_y[12], _15_y[13], _15_y[14], _15_y[15]);
  or or_4 (y_up_15, _15_y[16], _15_y[17], _15_y[18], _15_y[19], _15_y[20], _15_y[21], _15_y[22], _15_y[23], _15_y[24], _15_y[25], _15_y[26], _15_y[27], _15_y[28], _15_y[29], _15_y[30], _15_y[31]);
  or or_5 (y_down_16, _16_y[0], _16_y[1], _16_y[2], _16_y[3], _16_y[4], _16_y[5], _16_y[6], _16_y[7], _16_y[8], _16_y[9], _16_y[10], _16_y[11], _16_y[12], _16_y[13], _16_y[14], _16_y[15]);
  or or_6 (y_up_16, _16_y[16], _16_y[17], _16_y[18], _16_y[19], _16_y[20], _16_y[21], _16_y[22], _16_y[23], _16_y[24], _16_y[25], _16_y[26], _16_y[27], _16_y[28], _16_y[29], _16_y[30], _16_y[31]);
  or or_7 (y_down_17, _17_y[0], _17_y[1], _17_y[2], _17_y[3], _17_y[4], _17_y[5], _17_y[6], _17_y[7], _17_y[8], _17_y[9], _17_y[10], _17_y[11], _17_y[12], _17_y[13], _17_y[14], _17_y[15]);
  or or_8 (y_up_17, _17_y[16], _17_y[17], _17_y[18], _17_y[19], _17_y[20], _17_y[21], _17_y[22], _17_y[23], _17_y[24], _17_y[25], _17_y[26], _17_y[27], _17_y[28], _17_y[29], _17_y[30], _17_y[31]);
  not not_1 (not_1_out, y_up_13);
  not not_2 (not_2_out, y_up_15);
  not not_3 (not_3_out, y_up_16);
  not not_4 (not_4_out, y_up_18);
  not not_5 (not_5_out, y_up_14);
  not not_6 (not_6_out, y_up_17);
  and and_1 (is_0_up, not_1_out, not_5_out, not_2_out, not_3_out, not_6_out, not_4_out);
  or or_9 (y_down_13, _13_y[0], _13_y[1], _13_y[2], _13_y[3], _13_y[4], _13_y[5], _13_y[6], _13_y[7], _13_y[8], _13_y[9], _13_y[10], _13_y[11], _13_y[12], _13_y[13], _13_y[14], _13_y[15]);
  or or_10 (y_up_13, _13_y[16], _13_y[17], _13_y[18], _13_y[19], _13_y[20], _13_y[21], _13_y[22], _13_y[23], _13_y[24], _13_y[25], _13_y[26], _13_y[27], _13_y[28], _13_y[29], _13_y[30], _13_y[31]);
  or or_11 (y_down_18, _18_y[0], _18_y[1], _18_y[2], _18_y[3], _18_y[4], _18_y[5], _18_y[6], _18_y[7], _18_y[8], _18_y[9], _18_y[10], _18_y[11], _18_y[12], _18_y[13], _18_y[14], _18_y[15]);
  or or_12 (y_up_18, _18_y[16], _18_y[17], _18_y[18], _18_y[19], _18_y[20], _18_y[21], _18_y[22], _18_y[23], _18_y[24], _18_y[25], _18_y[26], _18_y[27], _18_y[28], _18_y[29], _18_y[30], _18_y[31]);

  // Notes on the sheet:
  //   можно ставить сверху
endmodule

module start_screen (
);

  DotMatrix #(.matrixcols(32), .matrixrows(32)) dotmatrix_1 (
    .col0({32{1'b0}}), .col1({32{1'b0}}), .col2({32{1'b0}}), .col3({32{1'b0}}), .col4(32'hfe3200),
    .col5(32'h904900), .col6(32'h904900), .col7(32'h602600), .col8({32{1'b0}}), .col9(32'hfe7f00),
    .col10(32'h904800), .col11(32'h904800), .col12(32'h6e3000), .col13({32{1'b0}}), .col14(32'hfe3f00),
    .col15(32'h924400), .col16(32'h924400), .col17(32'h923f00), .col18({32{1'b0}}), .col19(32'h641c00),
    .col20(32'h922200), .col21(32'h924100), .col22(32'h4c4100), .col23({32{1'b0}}), .col24(32'h647f00),
    .col25(32'h924900), .col26(32'h924900), .col27(32'h4c4900), .col28({32{1'b0}}), .col29({32{1'b0}}),
    .col30({32{1'b0}}), .col31({32{1'b0}}));
  // Probe on nothing
endmodule
